# Fritzing sketch Global Connections (saved by Fritzing 0.9.9b)

parts:
  Stepper_Driver_1 = DRV 8825 Stepper Motor Carrier, High Current [part_number="DRV 8825"]
  Stepper_Motor = Stepper Motor - Bipolar
  Battery_11_1V_4A_2_6Ah = LIPO-2000mAh [package=lipo-2000]
  Camera = TRANSCHIPTC5747 [package=camera_sfv24r-2st_2]
  Stepper_Driver_2 = DRV 8825 Stepper Motor Carrier, High Current [part_number="DRV 8825"]
  Stepper_Motor_2 = Stepper Motor - Bipolar
  Lidar = RPlidar A2M8 [package=THT]
  Buck_step_down_converter = RioRand LM2596
  J3 = Power Jack [package=power_jack_pth]
  Power_Protection = Resettable Fuse PTC [package=ptc-1206]
  IMU = InvenSense MPU6050
  Time_Of_Flight = Adafruit VL530X Time of Flight Distance Sensor [part_number="Adafruit #3317"]
  Power_sensor = INA 260
  Mod1 = Raspberry Pi 4B

nets:
  N1: Stepper_Driver_1.MS1, Stepper_Driver_2.MS1, Mod1.GPIO22
  N2: Stepper_Driver_1.MS2, Stepper_Driver_2.MS2, Mod1.GPIO23
  N3: Stepper_Driver_1.MS3, Stepper_Driver_2.MS3, Mod1.GPIO24
  VCC: Stepper_Driver_1.RESET, Stepper_Driver_1.SLEEP, Stepper_Driver_2.RESET, Stepper_Driver_2.SLEEP, Lidar.pin1, Buck_step_down_converter.Pin_3, Power_Protection.1, IMU.VCC, Time_Of_Flight.VCC, Power_sensor.VCC
  N4: Stepper_Driver_1.STEP, Mod1.GPIO5
  N5: Stepper_Driver_1.DIRECTION, Mod1.GPIO6
  N6: Stepper_Driver_1.VOLTAGE_ST/_MT, Stepper_Driver_2.VOLTAGE_ST/_MT, Buck_step_down_converter.Pin_1, J3.PWR, Power_sensor.IN+
  N7: Stepper_Driver_1.GROUND_ST/_MT, Battery_11_1V_4A_2_6Ah.-, Stepper_Driver_2.GROUND_ST/_MT, Buck_step_down_converter.Pin_2, J3.GNDBREAK, Power_sensor.IN-
  N8: Stepper_Driver_1.OUT_2B, Stepper_Motor_2.A
  N9: Stepper_Driver_1.OUT_2A, Stepper_Motor_2.C
  N10: Stepper_Driver_1.OUT_1A, Stepper_Motor_2.B
  N11: Stepper_Driver_1.OUT_1B, Stepper_Motor_2.D
  GND: Stepper_Driver_1.GROUND_LOG, Stepper_Driver_2.GROUND_LOG, Lidar.pin4, Buck_step_down_converter.Pin_4, IMU.GND, Time_Of_Flight.GND, Power_sensor.GND, Mod1.GND
  N12: Stepper_Motor.A, Stepper_Driver_2.OUT_2B
  N13: Stepper_Motor.C, Stepper_Driver_2.OUT_2A
  N14: Stepper_Motor.B, Stepper_Driver_2.OUT_1A
  N15: Stepper_Motor.D, Stepper_Driver_2.OUT_1B
  N16: Battery_11_1V_4A_2_6Ah.+, J3.GND
  N17: Camera.SCLK, Camera.DGND, Camera.DOUT_5
  N18: Stepper_Driver_2.STEP, Mod1.GPIO16
  N19: Stepper_Driver_2.DIRECTION, Mod1.GPIO19
  N20: Lidar.pin2, Mod1.GPIO15
  N21: Lidar.pin5, Mod1.GPIO12
  N22: Power_Protection.2, Mod1.5V
  N23: IMU.SCL, Time_Of_Flight.SCL, Power_sensor.SCL, Mod1.GPIO3
  N24: IMU.SDA, Time_Of_Flight.SDA, Power_sensor.SDA, Mod1.GPIO2

notes:
  Fontys AR minor
  Project RILey

custom parts:
  RPlidar A2M8: .The RPLIDAR A2 is the next generation low cost 360 degree 2D laser scanner (LIDAR) solution developed by SLAMTEC. It can take up to 4000 samples of laser ranging per second with high rotation speed. And equipped with SLAMTEC patented OPTMAG technology, it breakouts the life limitation of traditional LIDAR system so as to work stably for a long time.
  Adafruit VL530X Time of Flight Distance Sensor: The VL53L0X is a Time of Flight distance sensor like no other you've used! The sensor contains a very tiny invisible laser source, and a matching sensor. The VL53L0X can detect the "time of flight", or how long the light has taken to bounce back to the sensor. Since it uses a very narrow light source, it is good for determining distance of only the surface directly in front of it. Unlike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
  INA 260: Rev. B, add copy
